# Fritzing sketch Lunex (saved by Fritzing 0.9.3b)

parts:
  Raspberry_Pi_1 = Raspberry Pi 3 [part_number=RPI-3-V1.2]
  Composant1 = Arduino Uno (Rev3)
  J1 = Basic Servo
  hc-sr2 = hc-sr04
  J3 = screw terminal, 5 pins
  J2 = screw terminal, 5 pins
  J4 = Screw terminal - 2 pins [package=THT]

nets:
  GND: Raspberry_Pi_1.GND, Composant1.GND, J1.gnd, hc-sr2.GND, J3.pin1, J2.pin1, J4.pin1
  5V: Raspberry_Pi_1.5V, Composant1.VIN
  N1: Composant1.D8, J3.pin5
  N2: Composant1.D9_PWM, J2.pin4
  N3: Composant1.D10_PWM/SS, J3.pin4
  N4: Composant1.D11_PWM/MOSI, hc-sr2.Echo
  N5: Composant1.D12/MISO, hc-sr2.Trig
  N6: Composant1.D2, J2.pin3
  N7: Composant1.D3_PWM, J3.pin3
  N8: Composant1.D5_PWM, J1.pulse
  N9: Composant1.D7, J2.pin5
  VCC: Composant1.5V, J1.vcc, hc-sr2.VCC
  12V: J3.pin2, J4.pin2

custom parts:
  hc-sr04: This is a HC-SR04 Distance Sensor
